# Fritzing sketch LED_UNO_RGB_circuit (saved by Fritzing 0.9.2b)

parts:
  Part1 = Arduino Uno (Rev3) - ICSP
  LED1 = LEDs [package=led10mm]
  Q1 = npn-Powertransistor [package="TO220 [THT]"]
  R1 = Resistor [tolerance=±5% resistance=550 package="0603 [SMD]"]
  Q2 = npn-Powertransistor [package="TO220 [THT]"]
  R2 = Resistor [tolerance=±5% resistance=550 package="0603 [SMD]"]
  Q3 = npn-Powertransistor [package="TO220 [THT]"]
  R3 = Resistor [tolerance=±5% resistance=550 package="0603 [SMD]"]
  LED2 = LEDs [package=led10mm]
  LED3 = LEDs [package=led10mm]
  Part2 = Breakout Board for Electret Microphone
  C1 = Capacitor [package=cap-pth-small2]  # not connected

nets:
  N1: Part1.A0, Part2.AUD
  N2: Part1.D9_PWM, R3.Pin_1
  GND: Part1.GND, Q3.emitter, LED3.C, Part2.GND
  N3: Part1.D5_PWM, R1.Pin_1
  N4: Part1.D6_PWM, R2.Pin_1
  5V: Part1.5V, Part2.VCC
  N5: LED1.A, Q1.base, R1.Pin_0
  N6: Q2.base, R2.Pin_0, LED2.A
  N7: Q3.base, R3.Pin_0, LED3.A

notes:
  5mm LEDs
  To Strip
  12V
