# Fritzing sketch SketchLipoMonitor (saved by Fritzing 0.9.2b)

parts:
  Part1 = Arduino Uno (Rev3)
  U2 = LIPO-1000mAh [package=lipo-1000]
  U3 = LIPO-1000mAh [package=lipo-1000]
  U4 = LIPO-1000mAh [package=lipo-1000]
  U1 = LIPO-1000mAh [package=lipo-1000]
  R1 = Resistor [tolerance=±5% resistance=100k package=THT]
  R2 = Resistor [tolerance=±5% resistance=100k package=THT]
  R3 = Resistor [tolerance=±5% resistance=100k package=THT]
  R4 = Resistor [tolerance=±5% resistance=100k package=THT]
  R5 = Resistor [tolerance=±20% resistance=100k package=THT]
  R6 = Resistor [tolerance=±5% resistance=100k package=THT]
  R7 = Resistor [tolerance=±20% resistance=100k package=THT]
  R8 = Resistor [tolerance=±20% resistance=100k package=THT]
  R9 = Resistor [tolerance=±20% resistance=100k package=THT]  # not connected
  J1 = Piezo Speaker
  K1 = Relay [part_number=FRS1B-S package=THT]
  K2 = Relay [part_number=FRS1B-S package=THT]
  K3 = Relay [part_number=FRS1B-S package=THT]
  K4 = Relay [part_number=FRS1B-S package=THT]
  K5 = Relay [part_number=FRS1B-S package=THT]
  K6 = Relay [part_number=FRS1B-S package=THT]
  K7 = Relay [part_number=FRS1B-S package=THT]
  K8 = Relay [part_number=FRS1B-S package=THT]
  Power_plug1 = Power plug
  K9 = Relay [part_number=FRS1B-S package=THT]

nets:
  N1: Part1.A0, U3.-, U4.+, K6.B, K7.B
  N2: Part1.A1, R1.Pin_1
  N3: Part1.A2, R3.Pin_1, R4.Pin_0
  N4: Part1.A3, R5.Pin_1, R6.Pin_0
  N5: Part1.D8, K6.COIL1
  N6: Part1.D9_PWM, J1.pin2
  N7: Part1.D10_PWM/SS, K7.COIL1
  N8: Part1.D11_PWM/MOSI, K8.COIL1
  N9: Part1.D12/MISO, K9.COIL2
  N10: Part1.GND, U4.-, R2.Pin_1, R6.Pin_1, J1.pin1, K1.COIL2, K2.COIL2, K3.COIL2, K4.COIL2, K5.COIL2, K6.COIL2, K7.COIL2, K8.COIL2, K8.B
  N11: Part1.D3_PWM, K1.COIL1
  N12: Part1.D4, K2.COIL1
  N13: Part1.D5_PWM, K3.COIL1
  N14: Part1.D6_PWM, K4.COIL1
  N15: Part1.D7, K5.COIL1
  N16: U2.+, U1.-, R7.Pin_0, K2.B, K3.B
  N17: U2.-, U3.+, R1.Pin_0, K4.B, K5.B
  N18: U1.+, K1.B
  N19: R3.Pin_0, R7.Pin_1
  N20: R5.Pin_0, R8.Pin_1
  N21: K1.A, K3.A, K5.A, K7.A
  N22: K2.A, K4.A, K6.A, K8.A
  N23: Power_plug1.VCC, K9.B

notes:
  3.7V
  7.4V
  11.1V
  14.8V
  6V DC
  Buck Converter
  Warning: Arduino GND and Buck Converter GND must be mutually exclusive
