# Fritzing sketch Sketch_rocket_control (saved by Fritzing 0.9.3b)

parts:
  Part1 = Arduino Pro Mini (3.3V)
  Part2 = InvenSense MPU6050
  J1 = Basic Servo
  J2 = Basic Servo
  VCC1 = 4 x AAA Battery Mount
  VCC2 = Battery

nets:
  GND: Part1.GND, Part2.GND, J1.gnd, J2.gnd, VCC1.-, VCC2.-
  VCC: Part1.VCC, Part2.VCC, VCC2.+
  N1: Part1.A3, Part2.SCL
  N2: Part1.A2, Part2.SDA
  N3: Part1.D9, J1.pulse
  N4: Part1.D8, J2.pulse
  VCC_2: J1.vcc, J2.vcc, VCC1.+

notes:
  3.3V
  5V(or whatever servo needs)
  X-axis Control
  Z-axis Control
  Y-axis towards sky
  X-axis along the movement of servo on pin 8
  Z-axis along the movement of servo on pin 9
